# Fritzing sketch variationsDiagram (saved by Fritzing 0.9.3b)
breadboards: 1

parts:
  Part1 = Arduino 101
  S1 = Pushbutton [package="[SMD]"]
  S2 = Pushbutton [package="[SMD]"]
  S3 = Pushbutton [package="[SMD]"]
  S4 = Pushbutton [package="[SMD]"]
  S5 = Pushbutton [package="[SMD]"]
  S6 = Pushbutton [package="[SMD]"]

nets:
  N1: Part1.D8, S2.Pin_3, S2.Pin_4
  N2: Part1.D9_PWM, S3.Pin_3, S3.Pin_4
  N3: Part1.D10_PWM/SS, S4.Pin_3, S4.Pin_4
  N4: Part1.D11_PWM/MOSI, S5.Pin_3, S5.Pin_4
  N5: Part1.D12/MISO, S6.Pin_3, S6.Pin_4
  N6: Part1.GND, S1.Pin_1, S1.Pin_2, S2.Pin_1, S2.Pin_2, S3.Pin_1, S3.Pin_2, S4.Pin_1, S4.Pin_2, S5.Pin_1, S5.Pin_2, S6.Pin_1, S6.Pin_2
  N7: Part1.D7, S1.Pin_3, S1.Pin_4

custom parts:
  Arduino 101: A learning and development board that delivers the performance and low-power consumption of the Intel® Curie™ Module with the simplicity of Arduino at an entry-level price. It keeps the same robust form factor and peripheral list of the UNO with the addition of onboard Bluetooth LE capabilities and a 6-axis accelerometer/gyro to help you easily expand your creativity into the connected world.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
